# Fritzing sketch gps_gsm2 (saved by Fritzing 0.9.2b)
breadboards: 1

parts:
  Part1 = Arduino Pro Mini v13
  Part2 = SKM53
  Part3 = SIM900A Mini
  J1 = Power Jack [package=power_jack_slot]
  Part4 = SIM900A Mini
  LED1 = smd LED [color="Red (633nm)" package="0805 [SMD]"]
  R1 = Resistor [tolerance=±5% resistance=220 package="2010 [SMD]"]

nets:
  VCC: Part1.VCC, Part2.VCC, Part3.VCC, Part4.+3.7V_OUT
  GND: Part1.GND, Part2.GND, Part3.GND, Part4.GND_OUT, R1.Pin_1
  N1: Part1.D9_PWM, Part3.RX
  N2: Part1.D8, Part3.TX
  N3: Part1.D3_PWM, LED1.anode
  N4: Part1.D1/RX, Part2.TXD
  N5: Part1.D0/TX, Part2.RXD
  N6: J1.GND, Part4.GND_IN
  N7: J1.PWR, Part4.+12V_IN
  N8: LED1.cathode, R1.Pin_0

notes:
  TX / RX
