# Fritzing sketch gps_gsm (saved by Fritzing 0.9.2b)
breadboards: 1

parts:
  Part1 = Arduino Pro Mini v13
  Part2 = SKM53
  J1 = Power Jack [package=power_jack_slot]
  Part4 = SIM900A Mini
  LED1 = smd LED [color="Red (633nm)" package="0805 [SMD]"]
  R1 = Resistor [tolerance=±5% resistance=220 package="2010 [SMD]"]
  Part3 = SIM900A Mini
  R2 = Resistor [tolerance=±5% resistance=470 package="2010 [SMD]"]

nets:
  VCC: Part1.VCC, Part2.VCC, Part4.+3.7V_OUT, Part3.VCC
  GND: Part1.GND, Part2.GND, Part4.GND_OUT, R1.Pin_1, Part3.GND
  N1: Part1.D9_PWM, Part3.RX
  N2: Part1.D8, Part3.TX
  N3: Part1.D6_PWM, R2.Pin_0
  N4: Part1.D3_PWM, LED1.anode
  N5: Part1.D1/RX, Part2.TXD
  N6: Part1.D0/TX, Part2.RXD
  N7: J1.GND, Part4.GND_IN
  N8: J1.PWR, Part4.+12V_IN
  N9: LED1.cathode, R1.Pin_0
  N10: Part3.RST, R2.Pin_1

notes:
  TX / RX
